// Digital circuit multiplicador_8bits.dig as structural Verilog
module multiplicador_8bits (
  input  [7:0] AC,
  input  [7:0] N,
  output [7:0] AC_out,
  output [7:0] MQ_out,
  output OF
);

  wire soma_16bits_1_p4, soma_16bits_2_p4, soma_16bits_3_p4, soma_16bits_4_p4, soma_16bits_5_p4,
       soma_16bits_6_p4;
  wire [7:0] and_1_out, and_8_out;
  wire [8:1] and_2_out;
  wire [9:2] and_3_out;
  wire [10:3] and_4_out;
  wire [11:4] and_5_out;
  wire [12:5] and_6_out;
  wire [13:6] and_7_out;

  assign and_1_out = AC & {8{N[0]}};  // And and_1, 8 bits wide
  assign and_2_out = AC & {8{N[1]}};  // And and_2, 8 bits wide
  // soma_16bits soma_16bits_1: pin names not known; wires that end beside it: {{8{1'b0}}, and_1_out}, {{7{1'b0}}, and_2_out, 1'b0}, {8{1'b0}}, soma_16bits_1_p4
  assign and_3_out = AC & {8{N[2]}};  // And and_3, 8 bits wide
  assign and_4_out = AC & {8{N[3]}};  // And and_4, 8 bits wide
  // soma_16bits soma_16bits_2: pin names not known; wires that end beside it: soma_16bits_1_p4, {{6{1'b0}}, and_3_out, 2'b00}, {8{1'b0}}, soma_16bits_2_p4
  assign and_5_out = AC & {8{N[4]}};  // And and_5, 8 bits wide
  // soma_16bits soma_16bits_3: pin names not known; wires that end beside it: soma_16bits_2_p4, {{5{1'b0}}, and_4_out, 3'b000}, {8{1'b0}}, soma_16bits_3_p4
  assign and_6_out = AC & {8{N[5]}};  // And and_6, 8 bits wide
  // soma_16bits soma_16bits_4: pin names not known; wires that end beside it: soma_16bits_3_p4, {4'b0000, and_5_out, 4'b0000}, {8{1'b0}}, soma_16bits_4_p4
  assign and_7_out = AC & {8{N[6]}};  // And and_7, 8 bits wide
  // soma_16bits soma_16bits_5: pin names not known; wires that end beside it: soma_16bits_4_p4, {3'b000, and_6_out, {5{1'b0}}}, {8{1'b0}}, soma_16bits_5_p4
  assign and_8_out = AC & {8{N[7]}};  // And and_8, 8 bits wide
  // soma_16bits soma_16bits_6: pin names not known; wires that end beside it: soma_16bits_5_p4, {2'b00, and_7_out, {6{1'b0}}}, {8{1'b0}}, soma_16bits_6_p4
  // soma_16bits soma_16bits_7: pin names not known; wires that end beside it: soma_16bits_6_p4, {1'b0, and_8_out, {7{1'b0}}}, {8{1'b0}}, {MQ_out, AC_out}, OF
  // Pins of 1 and 8 bits meet at AC_out
  // Pins of 1 and 8 bits meet at MQ_out
  // Pins of 5 and 8 bits meet at {8{1'b0}}
endmodule
