// Digital circuit soma_16bits.dig as structural Verilog
module soma_16bits (
  input  [15:0] A,
  input  [15:0] B,
  input  Cin,
  output [15:0] S__16b,
  output OF
);

  wire OF_1;

  // soma_8bits soma_8bits_1: pin names not known; wires that end beside it: A[7:0], B[7:0], Cin, S__16b[7:0], OF_1
  // soma_8bits soma_8bits_2: pin names not known; wires that end beside it: A[15:8], B[15:8], OF_1, S__16b[15:8], OF
  // Pins of 1 and 16 bits meet at S__16b

  // Other names for the same wires on the sheet: A0_7[7:0] = A[7:0]; A8_15[7:0] = A[15:8]; B0_7[7:0] = B[7:0];
  //   B8_15[7:0] = B[15:8]; OF_2 = OF; S1[7:0] = S__16b[7:0]; S2[7:0] = S__16b[15:8]
endmodule
